// Logisim project 7조 Term project.circ as structural Verilog: 1 circuit, main circuit main
module main (
  input  in_1,
  input  in_2
);

  wire ADD, AND, BUN, CLOCK, D0, D0T4_out, D1, D1T4_out, D2, D2T4_out, D3, D4, d_ff_1_q, decoder_1_out0,
       decoder_1_out1, decoder_1_out2, decoder_1_out4, decoder_1_out5, LD_DR, LDA, or_1_out, or_2_out,
       or_7_out, STA, X7_out;
  wire [2:0] select, sequence_counter_q;
  wire [4:0] AR_q, PC_q;
  wire [7:0] AC_out, adder_1_out, and_1_out, BUS, DR_out, IR_q, multiplexer_1_out, ram_1_data;
  wire [7:5] undriven, undriven_2;

  Adder adder_1 (.a(DR_out), .b(AC_out), .out(adder_1_out), .cout(in_2));  // open: cin
  assign and_1_out = AC_out & DR_out;  // AND_Gate and_1, 8 bits wide
  Multiplexer #(.select(2), .width(8)) multiplexer_1 (
    .in0(DR_out), .in1(and_1_out), .in2(adder_1_out), .out(multiplexer_1_out), .sel({ADD, AND}));  // open: in3, en
  Counter #(.width(3), .max('h7)) sequence_counter (
    .Q(sequence_counter_q), .clk(CLOCK), .clr(d_ff_1_q));  // open: load, D, count, carry
  Decoder #(.select(3)) decoder_1 (
    .out0(decoder_1_out0), .out1(decoder_1_out1), .out2(decoder_1_out2), .out4(decoder_1_out4),
    .out5(decoder_1_out5), .sel(sequence_counter_q));  // open: out3, out6, out7, en
  D_Flip_Flop d_ff_1 (.clk(CLOCK), .D(or_1_out), .Q(d_ff_1_q));  // open: Qn, preset, en, reset
  or or_1 (or_1_out, STA, AND, BUN, LDA, ADD);
  and D0T4 (D0T4_out, D0, decoder_1_out4);
  and D1T4 (D1T4_out, D1, decoder_1_out4);
  and D2T4 (D2T4_out, D2, decoder_1_out4);
  and D4T4 (BUN, D4, decoder_1_out4);
  and D3T4 (STA, D3, decoder_1_out4);
  and D2T5 (LDA, D2, decoder_1_out5);
  and D0T5 (AND, D0, decoder_1_out5);
  and D1T5 (ADD, D1, decoder_1_out5);
  or or_2 (or_2_out, AND, ADD, LDA);
  or X7 (X7_out, D1T4_out, D0T4_out, D2T4_out, decoder_1_out1);
  or or_3 (LD_DR, D2T4_out, D0T4_out, D1T4_out);
  or or_4 (select[0], X7_out, LDA, BUN, decoder_1_out2);
  or or_5 (select[1], decoder_1_out0, X7_out, LDA);
  or or_6 (select[2], STA, X7_out, decoder_1_out2);
  or or_7 (or_7_out, decoder_1_out2, decoder_1_out0);
  Register #(.width(5)) AR (.D(BUS[4:0]), .en(or_7_out), .Q(AR_q), .clk(CLOCK), .clr(in_1));
  Counter #(.width(5), .max('h1f)) PC (
    .load(BUN), .D(BUS[4:0]), .count(decoder_1_out1), .Q(PC_q), .clk(CLOCK), .clr(in_1));  // open: carry
  Register DR (.D(BUS), .en(LD_DR), .Q(DR_out), .clk(CLOCK), .clr(in_1));
  Register IR (.D(BUS), .en(decoder_1_out1), .Q(IR_q), .clk(CLOCK), .clr(in_1));
  Register AC (.D(multiplexer_1_out), .en(or_2_out), .Q(AC_out), .clk(CLOCK), .clr(in_1));
  Clock clock_1 (.out(CLOCK));
  RAM #(.addrWidth(5), .bus("separate")) ram_1 (
    .addr(AR_q), .din(BUS), .data(ram_1_data), .str(STA), .clk(CLOCK), .ld(X7_out), .clr(in_1));  // open: sel
  Decoder #(.select(3)) decoder_2 (
    .out0(D0), .out1(D1), .out2(D2), .out3(D3), .out4(D4), .sel(IR_q[7:5]));  // open: out5, out6, out7, en
  Multiplexer #(.select(3), .width(8)) multiplexer_2 (
    .in1({undriven_2, AR_q}), .in2({undriven, PC_q}), .in3(DR_out), .in4(AC_out), .in5(IR_q),
    .in7(ram_1_data), .out(BUS), .sel(select));  // open: in0, in6, en

  // Notes on the sheet:
  //   타이밍
  //   CLEAR
endmodule
